# Fritzing sketch led (saved by Fritzing 0.9.3b)

parts:
  R1 = BBC MicroBit  # not connected
  CLIP1 = Alligator Clip
  CLIP2 = Alligator Clip
  LED1 = LED - 3mm [color="Red (633nm)" package="3 mm [THT]"]  # not connected
  CLIP3 = Alligator Clip
  CLIP4 = Alligator Clip

nets:
  N1: CLIP1.wire, CLIP3.wire
  N2: CLIP2.wire, CLIP4.wire

custom parts:
  BBC MicroBit: The BBC MICRO:BIT
  Alligator Clip: Alligator clip
  Alligator Clip: Alligator clip
